// Logisim project CPUv2.circ as structural Verilog: 25 circuits, main circuit mem_data
module mem_data (
  input  [3:0] icode,
  input  [63:0] valA,
  input  [63:0] valP,
  output [63:0] data_in
);

  wire decoder_1_out8;

  Decoder #(.select(4)) decoder_1 (
    .out8(decoder_1_out8), .sel(icode));  // open: out0, out1, out2, out3, out4, out5, out6, out7, out9, out10, out11, out12, out13, out14, out15, en
  Multiplexer #(.width(64)) multiplexer_1 (.in0(valA), .in1(valP), .out(data_in), .sel(decoder_1_out8));
endmodule

module mem_addr (
  input  [3:0] icode,
  input  [63:0] valA,
  input  [63:0] valE,
  output [63:0] addr_out
);

  wire decoder_1_out9, decoder_1_out11, or_1_out;

  Decoder #(.select(4)) decoder_1 (
    .out9(decoder_1_out9), .out11(decoder_1_out11), .sel(icode));  // open: out0, out1, out2, out3, out4, out5, out6, out7, out8, out10, out12, out13, out14, out15, en
  or or_1 (or_1_out, decoder_1_out11, decoder_1_out9);
  Multiplexer #(.width(64)) multiplexer_1 (.in0(valE), .in1(valA), .out(addr_out), .sel(or_1_out));
endmodule

module mem_read (
  input  [3:0] icode,
  output read
);

  wire decoder_1_out5, decoder_1_out9, decoder_1_out11;

  Decoder #(.select(4)) decoder_1 (
    .out5(decoder_1_out5), .out9(decoder_1_out9), .out11(decoder_1_out11), .sel(icode));  // open: out0, out1, out2, out3, out4, out6, out7, out8, out10, out12, out13, out14, out15, en
  or or_1 (read, decoder_1_out11, decoder_1_out9, decoder_1_out5);
endmodule

module mem_write (
  input  [3:0] icode,
  output write
);

  wire decoder_1_out4, decoder_1_out8, decoder_1_out10;

  Decoder #(.select(4)) decoder_1 (
    .out4(decoder_1_out4), .out8(decoder_1_out8), .out10(decoder_1_out10), .sel(icode));  // open: out0, out1, out2, out3, out5, out6, out7, out9, out11, out12, out13, out14, out15, en
  or or_1 (write, decoder_1_out10, decoder_1_out8, decoder_1_out4);
endmodule

module memory (
  input  [3:0] icode,
  input  [63:0] valA,
  input  [63:0] valP,
  input  [63:0] valE,
  input  clk,
  input  enable,
  output [63:0] valM
);

  wire and_1_out, mem_read_1_read, mem_write_1_write, not_1_out;
  wire [3:0] counter_1_q;
  wire [7:0] mem_data_1_data_in, mem_data_1_data_in_2, mem_data_1_data_in_3, mem_data_1_data_in_4,
       mem_data_1_data_in_5, mem_data_1_data_in_6, mem_data_1_data_in_7, mem_data_1_data_in_8,
       multiplexer_1_out, ram_1_dout;
  wire [11:0] adder_1_out;
  wire [63:0] mem_addr_1_addr_out;

  not not_1 (not_1_out, enable);
  mem_addr mem_addr_1 (.icode(icode), .valA(valA), .valE(valE), .addr_out(mem_addr_1_addr_out));
  mem_write mem_write_1 (.icode(icode), .write(mem_write_1_write));
  mem_read mem_read_1 (.icode(icode), .read(mem_read_1_read));
  and and_1 (and_1_out, clk, enable);
  mem_data mem_data_1 (
    .icode(icode), .valA(valA), .valP(valP),
    .data_in({mem_data_1_data_in_8, mem_data_1_data_in_7, mem_data_1_data_in_6, mem_data_1_data_in_5, mem_data_1_data_in_4, mem_data_1_data_in_3, mem_data_1_data_in_2, mem_data_1_data_in}));
  Adder #(.width(12)) adder_1 (
    .a(mem_addr_1_addr_out[11:0]), .b({{8{1'b0}}, counter_1_q}), .out(adder_1_out));  // open: cin, cout
  Counter #(.max('h7), .width(4)) counter_1 (
    .clr(not_1_out), .clk(and_1_out), .Q(counter_1_q));  // open: load, up, count, D, carry
  RAM #(.addrWidth(12)) ram_1 (
    .addr(adder_1_out), .we(mem_write_1_write), .oe(mem_read_1_read), .clk(and_1_out),
    .din(multiplexer_1_out), .dout(ram_1_dout));
  Multiplexer #(.select(4), .width(8)) multiplexer_1 (
    .in0(mem_data_1_data_in_8), .in1(mem_data_1_data_in_7), .in2(mem_data_1_data_in_6),
    .in3(mem_data_1_data_in_5), .in4(mem_data_1_data_in_4), .in5(mem_data_1_data_in_3),
    .in6(mem_data_1_data_in_2), .in7(mem_data_1_data_in), .out(multiplexer_1_out), .sel(counter_1_q));  // open: in8, in9, in10, in11, in12, in13, in14, in15
  Register register_1 (.D(ram_1_dout), .clk(and_1_out), .Q(valM[7:0]));  // open: en, clr
  Register register_2 (.D(valM[7:0]), .clk(and_1_out), .Q(valM[15:8]));  // open: en, clr
  Register register_3 (.D(valM[15:8]), .clk(and_1_out), .Q(valM[23:16]));  // open: en, clr
  Register register_4 (.D(valM[23:16]), .clk(and_1_out), .Q(valM[31:24]));  // open: en, clr
  Register register_5 (.D(valM[31:24]), .clk(and_1_out), .Q(valM[39:32]));  // open: en, clr
  Register register_6 (.D(valM[39:32]), .clk(and_1_out), .Q(valM[47:40]));  // open: en, clr
  Register register_7 (.D(valM[47:40]), .clk(and_1_out), .Q(valM[55:48]));  // open: en, clr
  Register register_8 (.D(valM[55:48]), .clk(and_1_out), .Q(valM[63:56]));  // open: en, clr
endmodule

module main (
  output [3:0] icode,
  output [63:0] valA,
  output cnd,
  output [63:0] valM,
  output [3:0] ifun,
  output [63:0] valB,
  output [63:0] valE,
  output [63:0] out_8,
  output [3:0] rA,
  output [3:0] rB,
  output [63:0] valC,
  output [63:0] valP,
  output [63:0] PC
);

  wire and_1_out, and_2_out, clock_1_out, comparator_1_eq, comparator_1_lt, DecodeEnable_bet,
       ExecuteEnable_bet, feeeetch_1_halt, FetchEnable_bet, MemoryEnable_bet, not_1_out, or_1_out, or_2_out,
       PCUpdateEnable_bet, WriteBackEnable_bet;
  wire [11:0] counter_1_q;

  Clock clock_1 (.out(clock_1_out));
  not not_1 (not_1_out, and_2_out);
  Counter #(.max('h3b), .width(12)) counter_1 (
    .clk(and_1_out), .Q(counter_1_q));  // open: clr, load, up, count, D, carry
  and and_1 (and_1_out, clock_1_out, not_1_out);
  Comparator #(.width(12)) comparator_1 (
    .a(12'ha), .b(counter_1_q), .eq(comparator_1_eq), .lt(comparator_1_lt));  // open: gt
  feeeetch feeeetch_1 (
    .PC(out_8), .clk(and_1_out), .enable(FetchEnable_bet), .icode(icode), .ifun(ifun), .rA(rA), .rB(rB),
    .valC(valC), .valP(valP), .Halt(feeeetch_1_halt));
  and and_2 (and_2_out, feeeetch_1_halt, or_1_out);
  or or_1 (or_1_out, comparator_1_eq, comparator_1_lt);
  or or_2 (or_2_out, WriteBackEnable_bet, DecodeEnable_bet);
  between PCUpdateEnable (.less(12'h33), .val(counter_1_q), .greater(12'h32), .bet(PCUpdateEnable_bet));
  between WriteBackEnable (.less(12'h32), .val(counter_1_q), .greater(12'h28), .bet(WriteBackEnable_bet));
  between MemoryEnable (.less(12'h26), .val(counter_1_q), .greater(12'h1e), .bet(MemoryEnable_bet));
  between ExecuteEnable (.less(12'h15), .val(counter_1_q), .greater(12'h14), .bet(ExecuteEnable_bet));
  between DecodeEnable (.less(12'h14), .val(counter_1_q), .greater(12'ha), .bet(DecodeEnable_bet));
  between FetchEnable (.less(12'ha), .val(counter_1_q), .greater({12{1'b0}}), .bet(FetchEnable_bet));
  decode decode_1 (
    .icode(icode), .rA(rA), .rB(rB), .valM(valM), .valE(valE), .cnd(cnd), .clk(and_1_out), .enable(or_2_out),
    .writeenable(WriteBackEnable_bet), .valA(valA), .valB(valB));
  execute execute_1 (
    .icode(icode), .ifun(ifun), .valC(valC), .valA(valA), .valB(valB), .clk(and_1_out),
    .enable(ExecuteEnable_bet), .cnd(cnd), .valE(valE));
  memory memory_1 (
    .icode(icode), .valA(valA), .valP(valP), .valE(valE), .clk(and_1_out), .enable(MemoryEnable_bet),
    .valM(valM));
  pcupdate pcupdate_1 (
    .icode(icode), .Cnd(cnd), .valC(valC), .valM(valM), .valP(valP), .enable(PCUpdateEnable_bet),
    .clk(and_1_out), .PC(out_8));

  assign PC = out_8;
endmodule

module InstructionMemory (
  input  [11:0] PC,
  input  CLK,
  output [7:0] byte0,
  output [7:0] byte1,
  output [7:0] byte2,
  output [7:0] byte3,
  output [7:0] byte4,
  output [7:0] byte5,
  output [7:0] byte6,
  output [7:0] byte7,
  output [7:0] byte8,
  output [7:0] byte9
);

  wire [7:0] rom_1_data;
  wire [11:0] adder_1_out, counter_1_q;

  Counter #(.max('ha), .width(12)) counter_1 (.clk(CLK), .Q(counter_1_q));  // open: clr, load, up, count, D, carry
  Adder #(.width(12)) adder_1 (.a(PC), .b(counter_1_q), .out(adder_1_out));  // open: cin, cout
  ROM #(.addrWidth(12)) rom_1 (.addr(adder_1_out), .data(rom_1_data));
  Register register_1 (.D(rom_1_data), .clk(CLK), .Q(byte9));  // open: en, clr
  Register register_2 (.D(byte9), .clk(CLK), .Q(byte8));  // open: en, clr
  Register register_3 (.D(byte8), .clk(CLK), .Q(byte7));  // open: en, clr
  Register register_4 (.D(byte7), .clk(CLK), .Q(byte6));  // open: en, clr
  Register register_5 (.D(byte6), .clk(CLK), .Q(byte5));  // open: en, clr
  Register register_6 (.D(byte5), .clk(CLK), .Q(byte4));  // open: en, clr
  Register register_7 (.D(byte4), .clk(CLK), .Q(byte3));  // open: en, clr
  Register register_8 (.D(byte3), .clk(CLK), .Q(byte2));  // open: en, clr
  Register register_9 (.D(byte2), .clk(CLK), .Q(byte1));  // open: en, clr
  Register register_10 (.D(byte1), .clk(CLK), .Q(byte0));  // open: en, clr

  // Notes on the sheet:
  //   contents of rom_1 (hex, n*v repeats v):
  //   30 f0 a 7*0 30 f3 14 7*0 61 30 72 2a 7*0 30 f1 ad b 7*0 30 f1 fe ca
endmodule

module pcupdate (
  input  [3:0] icode,
  input  Cnd,
  input  [63:0] valC,
  input  [63:0] valM,
  input  [63:0] valP,
  input  enable,
  input  clk,
  output [63:0] PC
);

  wire and_1_out, and_2_out, decoder_1_out1, decoder_1_out2, decoder_1_out3, decoder_1_out4, decoder_1_out5,
       decoder_1_out6, decoder_1_out7, decoder_1_out8, decoder_1_out9, decoder_1_out10, decoder_1_out11,
       decoder_1_out12, or_1_out, or_2_out;
  wire [1:0] priority_encoder_1_out;
  wire [63:0] multiplexer_1_out;

  Decoder #(.select(4)) decoder_1 (
    .out1(decoder_1_out1), .out2(decoder_1_out2), .out3(decoder_1_out3), .out4(decoder_1_out4),
    .out5(decoder_1_out5), .out6(decoder_1_out6), .out7(decoder_1_out7), .out8(decoder_1_out8),
    .out9(decoder_1_out9), .out10(decoder_1_out10), .out11(decoder_1_out11), .out12(decoder_1_out12),
    .sel(icode));  // open: out0, out13, out14, out15, en
  or or_1 (or_1_out, decoder_1_out1, decoder_1_out2, decoder_1_out3, decoder_1_out4, decoder_1_out5, decoder_1_out6, decoder_1_out8, decoder_1_out10, decoder_1_out11, decoder_1_out12);
  and and_1 (and_1_out, decoder_1_out7, Cnd);
  and and_2 (and_2_out, decoder_1_out7, ~Cnd);  // AND_Gate
  or or_2 (or_2_out, or_1_out, and_2_out);
  Multiplexer #(.select(2), .width(64)) multiplexer_1 (
    .in0(valP), .in1(valM), .in2(valC), .out(multiplexer_1_out), .sel(priority_encoder_1_out));  // open: in3
  Priority_Encoder #(.select(2)) priority_encoder_1 (
    .in0(or_2_out), .in1(decoder_1_out9), .in2(and_1_out), .out(priority_encoder_1_out));  // open: in3, gs, en_out, en_in
  Register #(.width(64)) register_1 (.D(multiplexer_1_out), .en(enable), .clk(clk), .Q(PC));  // open: clr
endmodule

module feeeetch (
  input  [63:0] PC,
  input  clk,
  input  enable,
  output [3:0] icode,
  output [3:0] ifun,
  output [3:0] rA,
  output [3:0] rB,
  output [63:0] valC,
  output [63:0] valP,
  output Halt
);

  wire and_1_out;
  wire [3:0] multiplexer_2_out, multiplexer_2_out_2;
  wire [7:0] instructionmemory_1_byte2, instructionmemory_1_byte3, instructionmemory_1_byte4,
       instructionmemory_1_byte5, instructionmemory_1_byte6, instructionmemory_1_byte7,
       instructionmemory_1_byte8, instructionmemory_1_byte9;

  and and_1 (and_1_out, clk, enable);
  InstructionMemory instructionmemory_1 (
    .PC(PC[11:0]), .CLK(and_1_out), .byte0({icode, ifun}), .byte1({rA, rB}),
    .byte2(instructionmemory_1_byte2), .byte3(instructionmemory_1_byte3), .byte4(instructionmemory_1_byte4),
    .byte5(instructionmemory_1_byte5), .byte6(instructionmemory_1_byte6), .byte7(instructionmemory_1_byte7),
    .byte8(instructionmemory_1_byte8), .byte9(instructionmemory_1_byte9));
  Multiplexer #(.select(4), .width(64)) multiplexer_1 (
    .in3({instructionmemory_1_byte9, instructionmemory_1_byte8, instructionmemory_1_byte7, instructionmemory_1_byte6, instructionmemory_1_byte5, instructionmemory_1_byte4, instructionmemory_1_byte3, instructionmemory_1_byte2}),
    .in4({instructionmemory_1_byte9, instructionmemory_1_byte8, instructionmemory_1_byte7, instructionmemory_1_byte6, instructionmemory_1_byte5, instructionmemory_1_byte4, instructionmemory_1_byte3, instructionmemory_1_byte2}),
    .in5({instructionmemory_1_byte9, instructionmemory_1_byte8, instructionmemory_1_byte7, instructionmemory_1_byte6, instructionmemory_1_byte5, instructionmemory_1_byte4, instructionmemory_1_byte3, instructionmemory_1_byte2}),
    .in7({instructionmemory_1_byte8, instructionmemory_1_byte7, instructionmemory_1_byte6, instructionmemory_1_byte5, instructionmemory_1_byte4, instructionmemory_1_byte3, instructionmemory_1_byte2, rA, rB}),
    .in8({instructionmemory_1_byte8, instructionmemory_1_byte7, instructionmemory_1_byte6, instructionmemory_1_byte5, instructionmemory_1_byte4, instructionmemory_1_byte3, instructionmemory_1_byte2, rA, rB}),
    .out(valC), .sel(icode));  // open: in0, in1, in2, in6, in9, in10, in11, in12, in13, in14, in15
  Multiplexer #(.select(4), .width(8)) multiplexer_2 (
    .in0(8'h1), .in1(8'h1), .in2(8'h2), .in3(8'ha), .in4(8'ha), .in5(8'ha), .in6(8'h2), .in7(8'h9),
    .in8(8'h9), .in9(8'h1), .in10(8'h2), .in11(8'h2), .out({multiplexer_2_out_2, multiplexer_2_out}),
    .sel(icode));  // open: in12, in13, in14, in15
  Adder #(.width(64)) adder_1 (
    .a(PC), .b({{56{1'b0}}, multiplexer_2_out_2, multiplexer_2_out}), .out(valP));  // open: cin, cout
  Comparator #(.width(4)) comparator_1 (.a(icode), .b(4'b0000), .eq(Halt));  // open: gt, lt
endmodule

module execute (
  input  [3:0] icode,
  input  [3:0] ifun,
  input  [63:0] valC,
  input  [63:0] valA,
  input  [63:0] valB,
  input  clk,
  input  enable,
  output cnd,
  output [63:0] valE
);

  wire and_1_out, setcc_1_out_2;
  wire [1:0] alufun_1_out_3;
  wire [2:0] alu_1_cc, cc_1_out_4;
  wire [63:0] alu_1_vale, alua_1_out_4, alub_1_out_3;

  and and_1 (and_1_out, clk, enable);
  SetCC setcc_1 (.icode(icode), .out_2(setcc_1_out_2));
  ALUA alua_1 (.icode(icode), .valC(valC), .valA(valA), .out_4(alua_1_out_4));
  ALUB alub_1 (.icode(icode), .valB(valB), .out_3(alub_1_out_3));
  ALUfun alufun_1 (.icode(icode), .ifun(ifun), .out_3(alufun_1_out_3));
  ALU alu_1 (.ALUA(alua_1_out_4), .ALUB(alub_1_out_3), .ALUfun(alufun_1_out_3), .CC(alu_1_cc), .valE(alu_1_vale));
  CC cc_1 (.SetCC(setcc_1_out_2), .ALU(alu_1_cc), .clk(and_1_out), .out_4(cc_1_out_4));
  Register #(.width(64)) register_1 (.D(alu_1_vale), .en(enable), .clk(and_1_out), .Q(valE));  // open: clr
  cond cond_1 (.cc(cc_1_out_4), .ifun(ifun), .cnd(cnd));
endmodule

module ALUA (
  input  [3:0] icode,
  input  [63:0] valC,
  input  [63:0] valA,
  output [63:0] out_4
);

  Multiplexer #(.select(4), .width(64)) multiplexer_1 (
    .in2(valA), .in3(valC), .in4(valC), .in5(valC), .in6(valA), .in7(valC), .in8(64'h8), .in9(64'h8),
    .in10(64'h8), .in11(64'h8), .out(out_4), .sel(icode));  // open: in0, in1, in12, in13, in14, in15
endmodule

module ALUB (
  input  [3:0] icode,
  input  [63:0] valB,
  output [63:0] out_3
);

  Multiplexer #(.select(4), .width(64)) multiplexer_1 (
    .in2({64{1'b0}}), .in3({64{1'b0}}), .in4(valB), .in5(valB), .in6(valB), .in8(valB), .in10(valB),
    .in11(valB), .out(out_3), .sel(icode));  // open: in0, in1, in7, in9, in12, in13, in14, in15
endmodule

module SetCC (
  input  [3:0] icode,
  output out_2
);

  Comparator #(.width(4)) comparator_1 (.a(icode), .b(4'b0110), .eq(out_2));  // open: gt, lt
endmodule

module ALUfun (
  input  [3:0] icode,
  input  [3:0] ifun,
  output [1:0] out_3
);

  wire decoder_1_out2, decoder_1_out3, decoder_1_out4, decoder_1_out5, decoder_1_out6, decoder_1_out8,
       decoder_1_out9, decoder_1_out10, decoder_1_out11, decoder_2_out0, decoder_2_out1, decoder_2_out2,
       decoder_2_out3, or_1_out, or_2_out;

  Decoder #(.enable("false"), .select(4)) decoder_1 (
    .out2(decoder_1_out2), .out3(decoder_1_out3), .out4(decoder_1_out4), .out5(decoder_1_out5),
    .out6(decoder_1_out6), .out8(decoder_1_out8), .out9(decoder_1_out9), .out10(decoder_1_out10),
    .out11(decoder_1_out11), .sel(icode));  // open: out0, out1, out7, out12, out13, out14, out15
  Decoder #(.select(4)) decoder_2 (
    .out0(decoder_2_out0), .out1(decoder_2_out1), .out2(decoder_2_out2), .out3(decoder_2_out3), .sel(ifun),
    .en(decoder_1_out6));  // open: out4, out5, out6, out7, out8, out9, out10, out11, out12, out13, out14, out15
  or or_1 (or_1_out, decoder_1_out2, decoder_1_out3, decoder_1_out4, decoder_1_out5, decoder_1_out9, decoder_1_out11, decoder_2_out0);
  or or_2 (or_2_out, decoder_1_out8, decoder_1_out10, decoder_2_out1);
  Priority_Encoder #(.select(2)) priority_encoder_1 (
    .in0(or_1_out), .in1(or_2_out), .in2(decoder_2_out2), .in3(decoder_2_out3), .out(out_3));  // open: gs, en_out, en_in
endmodule

module ALU (
  input  [63:0] ALUA,
  input  [63:0] ALUB,
  input  [1:0] ALUfun,
  output [2:0] CC,
  output [63:0] valE
);

  wire comparator_2_gt, comparator_2_lt, comparator_3_eq, comparator_4_lt, or_1_out, subtractor_1_bout;
  wire [63:0] adder_1_out, and_1_out, subtractor_1_out, xor_1_out;

  Adder #(.width(64)) adder_1 (.a(ALUB), .b(ALUA), .out(adder_1_out));  // open: cin, cout
  Subtractor #(.width(64)) subtractor_1 (
    .a(ALUB), .b(ALUA), .out(subtractor_1_out), .bout(subtractor_1_bout));  // open: bin
  assign and_1_out = ALUB & ALUA;  // AND_Gate and_1, 64 bits wide
  assign xor_1_out = ALUB ^ ALUA;  // XOR_Gate xor_1, 64 bits wide
  Multiplexer #(.select(2), .width(64)) multiplexer_1 (
    .in0(adder_1_out), .in1(subtractor_1_out), .in2(and_1_out), .in3(xor_1_out), .out(valE), .sel(ALUfun));
  Comparator #(.width(64)) comparator_1 (.a(valE), .b({64{1'b0}}), .eq(CC[0]), .lt(CC[1]));  // open: gt
  Comparator #(.width(1)) comparator_2 (
    .a(CC[1]), .b(subtractor_1_bout), .gt(comparator_2_gt), .lt(comparator_2_lt));  // open: eq
  Comparator #(.width(1)) comparator_3 (
    .a(subtractor_1_bout), .b(comparator_4_lt), .eq(comparator_3_eq));  // open: gt, lt
  Comparator #(.width(64)) comparator_4 (.a(valE), .b({64{1'b0}}), .lt(comparator_4_lt));  // open: gt, eq
  or or_1 (or_1_out, comparator_2_gt, comparator_2_lt);
  and and_2 (CC[2], or_1_out, comparator_3_eq);

  // Notes on the sheet:
  //   Zero Flag
  //   Sign Flag
  //   Overflow Flag
endmodule

module CC (
  input  SetCC,
  input  [2:0] ALU,
  input  clk,
  output [2:0] out_4
);

  Register #(.width(3)) register_1 (.D(ALU), .en(SetCC), .clk(clk), .Q(out_4));  // open: clr
endmodule

module cond (
  input  [2:0] cc,
  input  [3:0] ifun,
  output cnd
);

  wire and_1_out, not_1_out, not_2_out, not_3_out, not_4_out, or_1_out, xor_1_out, xor_2_out, xor_3_out,
       xor_4_out;

  xor xor_1 (xor_1_out, cc[1], cc[0]);
  xor xor_2 (xor_2_out, cc[1], cc[0]);
  not not_1 (not_1_out, cc[2]);
  xor xor_3 (xor_3_out, cc[1], cc[0]);
  xor xor_4 (xor_4_out, cc[1], cc[0]);
  or or_1 (or_1_out, xor_1_out, cc[2]);
  not not_2 (not_2_out, xor_3_out);
  not not_3 (not_3_out, xor_4_out);
  not not_4 (not_4_out, cc[2]);
  and and_1 (and_1_out, not_3_out, not_4_out);
  Multiplexer #(.select(4)) multiplexer_1 (
    .in0(1'b1), .in1(or_1_out), .in2(xor_2_out), .in3(cc[2]), .in4(not_1_out), .in5(not_2_out),
    .in6(and_1_out), .out(cnd), .sel(ifun));  // open: in7, in8, in9, in10, in11, in12, in13, in14, in15
endmodule

module between (
  input  [11:0] less,
  input  [11:0] val,
  input  [11:0] greater,
  output bet
);

  wire comparator_1_gt, comparator_2_eq, comparator_2_gt, or_1_out;

  Comparator #(.width(12)) comparator_1 (.a(less), .b(val), .gt(comparator_1_gt));  // open: eq, lt
  Comparator #(.width(12)) comparator_2 (.a(val), .b(greater), .gt(comparator_2_gt), .eq(comparator_2_eq));  // open: lt
  or or_1 (or_1_out, comparator_2_gt, comparator_2_eq);
  and and_1 (bet, comparator_1_gt, or_1_out);
endmodule

module register_file (
  input  clk,
  input  [3:0] srcA,
  input  [3:0] srcB,
  input  [63:0] valM,
  input  [63:0] valE,
  input  [3:0] dstE,
  input  [3:0] dstM,
  input  writeenable,
  output [63:0] valA,
  output [63:0] valB
);

  wire and_1_out, and_2_out, and_3_out, and_4_out, decoder_1_out0, decoder_1_out1, decoder_1_out2,
       decoder_1_out3, decoder_1_out4, decoder_1_out5, decoder_1_out6, decoder_1_out7, decoder_1_out8,
       decoder_1_out9, decoder_1_out10, decoder_1_out11, decoder_1_out12, decoder_1_out13, decoder_1_out14,
       decoder_2_out0, decoder_2_out1, decoder_2_out2, decoder_2_out3, decoder_2_out4, decoder_2_out5,
       decoder_2_out6, decoder_2_out7, decoder_2_out8, decoder_2_out9, decoder_2_out10, decoder_2_out11,
       decoder_2_out12, decoder_2_out13, decoder_2_out14, decoder_3_out0, decoder_3_out1, decoder_3_out2,
       decoder_3_out3, decoder_3_out4, decoder_3_out5, decoder_3_out6, decoder_3_out7, decoder_3_out8,
       decoder_3_out9, decoder_3_out10, decoder_3_out11, decoder_3_out12, decoder_3_out13, decoder_3_out14,
       nand_1_out, nand_2_out, nand_3_out, nand_4_out, not_1_out, not_2_out, not_3_out, not_4_out, or_1_out;
  wire [3:0] controlled_buffer_2_out, controlled_buffer_36_out, controlled_buffer_37_out;
  wire [63:0] controlled_buffer_1_out, multiplexer_1_out, r8_q, r9_q, r10_q, r11_q, r12_q, r13_q, r14_q,
       rax_q, rbp_q, rbx_q, rcx_q, rdi_q, rdx_q, rsi_q, rsp_q;

  not not_1 (not_1_out, and_1_out);
  nand nand_1 (nand_1_out, dstE[0], dstE[1], dstE[2], dstE[3]);
  nand nand_2 (nand_2_out, dstM[0], dstM[1], dstM[2], dstM[3]);
  and and_1 (and_1_out, nand_1_out, nand_2_out);
  not not_2 (not_2_out, not_1_out);
  and and_2 (and_2_out, ~nand_1_out, ~nand_2_out);  // AND_Gate
  // Probe on multiplexer_1_out
  Decoder #(.enable("false"), .select(4)) decoder_1 (
    .out0(decoder_1_out0), .out1(decoder_1_out1), .out2(decoder_1_out2), .out3(decoder_1_out3),
    .out4(decoder_1_out4), .out5(decoder_1_out5), .out6(decoder_1_out6), .out7(decoder_1_out7),
    .out8(decoder_1_out8), .out9(decoder_1_out9), .out10(decoder_1_out10), .out11(decoder_1_out11),
    .out12(decoder_1_out12), .out13(decoder_1_out13), .out14(decoder_1_out14), .sel(controlled_buffer_2_out));  // open: out15
  and and_3 (and_3_out, writeenable, clk);
  assign controlled_buffer_1_out = and_4_out ? valE : 64'bz;  // Controlled_Buffer controlled_buffer_1
  and and_4 (and_4_out, nand_1_out, ~nand_2_out);  // AND_Gate
  assign controlled_buffer_2_out = and_4_out ? dstE : 4'bz;  // Controlled_Buffer controlled_buffer_2
  assign controlled_buffer_2_out = nand_2_out ? dstM : 4'bz;  // Controlled_Buffer controlled_buffer_3
  or or_1 (or_1_out, not_2_out, decoder_1_out4);
  assign controlled_buffer_1_out = nand_2_out ? valM : 64'bz;  // Controlled_Buffer controlled_buffer_4
  assign controlled_buffer_2_out = and_2_out ? 4'b1111 : 4'bz;  // Controlled_Buffer controlled_buffer_5
  Multiplexer #(.width(64)) multiplexer_1 (
    .in0(valE), .in1(controlled_buffer_1_out), .out(multiplexer_1_out), .sel(not_1_out));
  Register #(.width(64)) rax (
    .D(controlled_buffer_1_out), .en(decoder_1_out0), .clk(and_3_out), .Q(rax_q));  // open: clr
  Register #(.width(64)) rcx (
    .D(controlled_buffer_1_out), .en(decoder_1_out1), .clk(and_3_out), .Q(rcx_q));  // open: clr
  Register #(.width(64)) rdx (
    .D(controlled_buffer_1_out), .en(decoder_1_out2), .clk(and_3_out), .Q(rdx_q));  // open: clr
  Register #(.width(64)) rbx (
    .D(controlled_buffer_1_out), .en(decoder_1_out3), .clk(and_3_out), .Q(rbx_q));  // open: clr
  Register #(.width(64)) rsp (.D(multiplexer_1_out), .en(or_1_out), .clk(and_3_out), .Q(rsp_q));  // open: clr
  Register #(.width(64)) rbp (
    .D(controlled_buffer_1_out), .en(decoder_1_out5), .clk(and_3_out), .Q(rbp_q));  // open: clr
  Register #(.width(64)) rsi (
    .D(controlled_buffer_1_out), .en(decoder_1_out6), .clk(and_3_out), .Q(rsi_q));  // open: clr
  Register #(.width(64)) rdi (
    .D(controlled_buffer_1_out), .en(decoder_1_out7), .clk(and_3_out), .Q(rdi_q));  // open: clr
  Register #(.width(64)) r8 (.D(controlled_buffer_1_out), .en(decoder_1_out8), .clk(and_3_out), .Q(r8_q));  // open: clr
  Register #(.width(64)) r9 (.D(controlled_buffer_1_out), .en(decoder_1_out9), .clk(and_3_out), .Q(r9_q));  // open: clr
  Register #(.width(64)) r10 (
    .D(controlled_buffer_1_out), .en(decoder_1_out10), .clk(and_3_out), .Q(r10_q));  // open: clr
  Register #(.width(64)) r11 (
    .D(controlled_buffer_1_out), .en(decoder_1_out11), .clk(and_3_out), .Q(r11_q));  // open: clr
  Register #(.width(64)) r12 (
    .D(controlled_buffer_1_out), .en(decoder_1_out12), .clk(and_3_out), .Q(r12_q));  // open: clr
  Register #(.width(64)) r13 (
    .D(controlled_buffer_1_out), .en(decoder_1_out13), .clk(and_3_out), .Q(r13_q));  // open: clr
  Register #(.width(64)) r14 (
    .D(controlled_buffer_1_out), .en(decoder_1_out14), .clk(and_3_out), .Q(r14_q));  // open: clr
  assign valA = decoder_2_out0 ? rax_q : 64'bz;  // Controlled_Buffer controlled_buffer_6
  assign valB = decoder_3_out0 ? rax_q : 64'bz;  // Controlled_Buffer controlled_buffer_7
  assign valA = decoder_2_out1 ? rcx_q : 64'bz;  // Controlled_Buffer controlled_buffer_8
  assign valB = decoder_3_out1 ? rcx_q : 64'bz;  // Controlled_Buffer controlled_buffer_9
  assign valA = decoder_2_out2 ? rdx_q : 64'bz;  // Controlled_Buffer controlled_buffer_10
  assign valB = decoder_3_out2 ? rdx_q : 64'bz;  // Controlled_Buffer controlled_buffer_11
  assign valA = decoder_2_out3 ? rbx_q : 64'bz;  // Controlled_Buffer controlled_buffer_12
  assign valB = decoder_3_out3 ? rbx_q : 64'bz;  // Controlled_Buffer controlled_buffer_13
  assign valA = decoder_2_out4 ? rsp_q : 64'bz;  // Controlled_Buffer controlled_buffer_14
  assign valB = decoder_3_out4 ? rsp_q : 64'bz;  // Controlled_Buffer controlled_buffer_15
  assign valA = decoder_2_out5 ? rbp_q : 64'bz;  // Controlled_Buffer controlled_buffer_16
  assign valB = decoder_3_out5 ? rbp_q : 64'bz;  // Controlled_Buffer controlled_buffer_17
  assign valA = decoder_2_out6 ? rsi_q : 64'bz;  // Controlled_Buffer controlled_buffer_18
  assign valB = decoder_3_out6 ? rsi_q : 64'bz;  // Controlled_Buffer controlled_buffer_19
  assign valA = decoder_2_out7 ? rdi_q : 64'bz;  // Controlled_Buffer controlled_buffer_20
  assign valB = decoder_3_out7 ? rdi_q : 64'bz;  // Controlled_Buffer controlled_buffer_21
  assign valA = decoder_2_out8 ? r8_q : 64'bz;  // Controlled_Buffer controlled_buffer_22
  assign valB = decoder_3_out8 ? r8_q : 64'bz;  // Controlled_Buffer controlled_buffer_23
  assign valA = decoder_2_out9 ? r9_q : 64'bz;  // Controlled_Buffer controlled_buffer_24
  assign valB = decoder_3_out9 ? r9_q : 64'bz;  // Controlled_Buffer controlled_buffer_25
  assign valA = decoder_2_out10 ? r10_q : 64'bz;  // Controlled_Buffer controlled_buffer_26
  assign valB = decoder_3_out10 ? r10_q : 64'bz;  // Controlled_Buffer controlled_buffer_27
  assign valA = decoder_2_out11 ? r11_q : 64'bz;  // Controlled_Buffer controlled_buffer_28
  assign valB = decoder_3_out11 ? r11_q : 64'bz;  // Controlled_Buffer controlled_buffer_29
  assign valA = decoder_2_out12 ? r12_q : 64'bz;  // Controlled_Buffer controlled_buffer_30
  assign valB = decoder_3_out12 ? r12_q : 64'bz;  // Controlled_Buffer controlled_buffer_31
  assign valA = decoder_2_out13 ? r13_q : 64'bz;  // Controlled_Buffer controlled_buffer_32
  assign valB = decoder_3_out13 ? r13_q : 64'bz;  // Controlled_Buffer controlled_buffer_33
  assign valA = decoder_2_out14 ? r14_q : 64'bz;  // Controlled_Buffer controlled_buffer_34
  assign valB = decoder_3_out14 ? r14_q : 64'bz;  // Controlled_Buffer controlled_buffer_35
  Decoder #(.enable("false"), .select(4)) decoder_2 (
    .out0(decoder_2_out0), .out1(decoder_2_out1), .out2(decoder_2_out2), .out3(decoder_2_out3),
    .out4(decoder_2_out4), .out5(decoder_2_out5), .out6(decoder_2_out6), .out7(decoder_2_out7),
    .out8(decoder_2_out8), .out9(decoder_2_out9), .out10(decoder_2_out10), .out11(decoder_2_out11),
    .out12(decoder_2_out12), .out13(decoder_2_out13), .out14(decoder_2_out14), .sel(controlled_buffer_36_out));  // open: out15
  Decoder #(.enable("false"), .select(4)) decoder_3 (
    .out0(decoder_3_out0), .out1(decoder_3_out1), .out2(decoder_3_out2), .out3(decoder_3_out3),
    .out4(decoder_3_out4), .out5(decoder_3_out5), .out6(decoder_3_out6), .out7(decoder_3_out7),
    .out8(decoder_3_out8), .out9(decoder_3_out9), .out10(decoder_3_out10), .out11(decoder_3_out11),
    .out12(decoder_3_out12), .out13(decoder_3_out13), .out14(decoder_3_out14), .sel(controlled_buffer_37_out));  // open: out15
  not not_3 (not_3_out, nand_3_out);
  assign controlled_buffer_36_out = not_3_out ? 4'b1111 : 4'bz;  // Controlled_Buffer controlled_buffer_36
  assign controlled_buffer_37_out = not_4_out ? 4'b1111 : 4'bz;  // Controlled_Buffer controlled_buffer_37
  not not_4 (not_4_out, nand_4_out);
  assign controlled_buffer_36_out = nand_3_out ? srcA : 4'bz;  // Controlled_Buffer controlled_buffer_38
  assign controlled_buffer_37_out = nand_4_out ? srcB : 4'bz;  // Controlled_Buffer controlled_buffer_39
  nand nand_3 (nand_3_out, srcA[0], srcA[1], srcA[2], srcA[3]);
  nand nand_4 (nand_4_out, srcB[0], srcB[1], srcB[2], srcB[3]);
endmodule

module dstE (
  input  cnd,
  input  [3:0] icode,
  input  [3:0] rB,
  output [3:0] out_4
);

  wire and_1_out, decoder_1_out2, decoder_1_out3, decoder_1_out6, decoder_1_out8, decoder_1_out9,
       decoder_1_out10, decoder_1_out11, nor_1_out, or_1_out, or_2_out, or_3_out;

  Decoder #(.enable("false"), .select(4)) decoder_1 (
    .out2(decoder_1_out2), .out3(decoder_1_out3), .out6(decoder_1_out6), .out8(decoder_1_out8),
    .out9(decoder_1_out9), .out10(decoder_1_out10), .out11(decoder_1_out11), .sel(icode));  // open: out0, out1, out4, out5, out7, out12, out13, out14, out15
  and and_1 (and_1_out, cnd, decoder_1_out2);
  or or_1 (or_1_out, decoder_1_out3, decoder_1_out6);
  or or_2 (or_2_out, decoder_1_out8, decoder_1_out9, decoder_1_out10, decoder_1_out11);
  or or_3 (or_3_out, and_1_out, or_1_out);
  assign out_4 = or_3_out ? rB : 4'bz;  // Controlled_Buffer controlled_buffer_1
  nor nor_1 (nor_1_out, or_3_out, or_2_out);
  assign out_4 = nor_1_out ? 4'b1111 : 4'bz;  // Controlled_Buffer controlled_buffer_2
  assign out_4 = or_2_out ? 4'b0100 : 4'bz;  // Controlled_Buffer controlled_buffer_3
endmodule

module dstM (
  input  [3:0] icode,
  input  [3:0] rA,
  output [3:0] out_3
);

  wire decoder_1_out5, decoder_1_out11, not_1_out, or_1_out;

  Decoder #(.enable("false"), .select(4)) decoder_1 (
    .out5(decoder_1_out5), .out11(decoder_1_out11), .sel(icode));  // open: out0, out1, out2, out3, out4, out6, out7, out8, out9, out10, out12, out13, out14, out15
  or or_1 (or_1_out, decoder_1_out5, decoder_1_out11);
  not not_1 (not_1_out, or_1_out);
  assign out_3 = or_1_out ? rA : 4'bz;  // Controlled_Buffer controlled_buffer_1
  assign out_3 = not_1_out ? 4'b1111 : 4'bz;  // Controlled_Buffer controlled_buffer_2
endmodule

module srcA (
  input  [3:0] icode,
  input  [3:0] rA,
  output [3:0] out_3
);

  wire and_1_out, decoder_1_out2, decoder_1_out4, decoder_1_out5, decoder_1_out6, decoder_1_out8,
       decoder_1_out9, decoder_1_out10, decoder_1_out11, or_1_out, or_2_out;

  Decoder #(.enable("false"), .select(4)) decoder_1 (
    .out2(decoder_1_out2), .out4(decoder_1_out4), .out5(decoder_1_out5), .out6(decoder_1_out6),
    .out8(decoder_1_out8), .out9(decoder_1_out9), .out10(decoder_1_out10), .out11(decoder_1_out11),
    .sel(icode));  // open: out0, out1, out3, out7, out12, out13, out14, out15
  or or_1 (or_1_out, decoder_1_out8, decoder_1_out11, decoder_1_out9);
  or or_2 (or_2_out, decoder_1_out2, decoder_1_out4, decoder_1_out5, decoder_1_out6, decoder_1_out10);
  and and_1 (and_1_out, ~or_1_out, ~or_2_out);  // AND_Gate
  assign out_3 = and_1_out ? 4'b1111 : 4'bz;  // Controlled_Buffer controlled_buffer_1
  assign out_3 = or_2_out ? rA : 4'bz;  // Controlled_Buffer controlled_buffer_2
  assign out_3 = or_1_out ? 4'b0100 : 4'bz;  // Controlled_Buffer controlled_buffer_3
endmodule

module srcB (
  input  [3:0] icode,
  input  [3:0] rB,
  output [3:0] out_3
);

  wire and_1_out, decoder_1_out2, decoder_1_out3, decoder_1_out4, decoder_1_out5, decoder_1_out6,
       decoder_1_out8, decoder_1_out9, decoder_1_out10, decoder_1_out11, or_1_out, or_2_out;

  Decoder #(.enable("false"), .select(4)) decoder_1 (
    .out2(decoder_1_out2), .out3(decoder_1_out3), .out4(decoder_1_out4), .out5(decoder_1_out5),
    .out6(decoder_1_out6), .out8(decoder_1_out8), .out9(decoder_1_out9), .out10(decoder_1_out10),
    .out11(decoder_1_out11), .sel(icode));  // open: out0, out1, out7, out12, out13, out14, out15
  or or_1 (or_1_out, decoder_1_out2, decoder_1_out3, decoder_1_out4, decoder_1_out5, decoder_1_out6);
  or or_2 (or_2_out, decoder_1_out8, decoder_1_out9, decoder_1_out10, decoder_1_out11);
  and and_1 (and_1_out, ~or_1_out, ~or_2_out);  // AND_Gate
  assign out_3 = and_1_out ? 4'b1111 : 4'bz;  // Controlled_Buffer controlled_buffer_1
  assign out_3 = or_1_out ? rB : 4'bz;  // Controlled_Buffer controlled_buffer_2
  assign out_3 = or_2_out ? 4'b0100 : 4'bz;  // Controlled_Buffer controlled_buffer_3
endmodule

module decode (
  input  [3:0] icode,
  input  [3:0] rA,
  input  [3:0] rB,
  input  [63:0] valM,
  input  [63:0] valE,
  input  cnd,
  input  clk,
  input  enable,
  input  writeenable,
  output [63:0] valA,
  output [63:0] valB
);

  wire and_1_out;
  wire [3:0] dste_1_out_4, dstm_1_out_3, srca_1_out_3, srcb_1_out_3;

  and and_1 (and_1_out, clk, enable);
  dstE dste_1 (.cnd(cnd), .icode(icode), .rB(rB), .out_4(dste_1_out_4));
  dstM dstm_1 (.icode(icode), .rA(rA), .out_3(dstm_1_out_3));
  srcA srca_1 (.icode(icode), .rA(rA), .out_3(srca_1_out_3));
  register_file register_file_1 (
    .clk(and_1_out), .srcA(srca_1_out_3), .srcB(srcb_1_out_3), .valM(valM), .valE(valE), .dstE(dste_1_out_4),
    .dstM(dstm_1_out_3), .writeenable(writeenable), .valA(valA), .valB(valB));
  srcB srcb_1 (.icode(icode), .rB(rB), .out_3(srcb_1_out_3));
endmodule

module enable_counter (
  input  [5:0] lower,
  input  [5:0] upper,
  input  clk,
  output out_clk
);

  wire and_1_out, comparator_1_lt, comparator_2_gt, comparator_2_lt, not_1_out;
  wire [5:0] counter_10_q;

  Counter #(.max('h30), .width(6)) counter_10 (
    .clr(1'b0), .load(1'b0), .up(1'b1), .count(1'b1), .clk(not_1_out), .Q(counter_10_q));  // open: D, carry
  not not_1 (not_1_out, clk);
  // Probe on counter_10_q
  Comparator #(.mode("unsigned"), .width(6)) comparator_1 (
    .a(counter_10_q), .b(lower), .lt(comparator_1_lt));  // open: gt, eq
  Comparator #(.mode("unsigned"), .width(6)) comparator_2 (
    .a(counter_10_q), .b(upper), .gt(comparator_2_gt), .lt(comparator_2_lt));  // open: eq
  and and_1 (and_1_out, ~comparator_1_lt, ~comparator_2_gt);  // AND_Gate
  and and_2 (out_clk, and_1_out, clk);
endmodule
